// Logisim project main.circ as structural Verilog: 6 circuits, main circuit main
module main (
);

  wire button_1_out, clock_1_out;
  wire [4:0] joystick_1_y, kinematic_controller_1_ballx, kinematic_controller_1_bally,
       kinematic_controller_1_chipid, kinematic_controller_1_leftbaty_2, kinematic_controller_1_rightbaty,
       not_1_out, videosection_1_out_14, videosection_1_out_15, videosection_1_out_16, videosection_1_out_17,
       videosection_1_out_18, videosection_2_out_14, videosection_2_out_15, videosection_2_out_16,
       videosection_2_out_17, videosection_2_out_18, videosection_3_out_14, videosection_3_out_15,
       videosection_3_out_16, videosection_3_out_17, videosection_3_out_18;
  wire [31:0] videosection_1__1, videosection_1__2, videosection_1__3, videosection_1__3_2,
       videosection_1__4, videosection_1__5, videosection_1__6, videosection_1__7, videosection_2__1,
       videosection_2__2, videosection_2__3, videosection_2__3_2, videosection_2__4, videosection_2__5,
       videosection_2__6, videosection_2__7, videosection_3__1, videosection_3__2, videosection_3__3,
       videosection_3__3_2, videosection_3__4, videosection_3__5, videosection_3__6, videosection_3__7,
       videosection_4__1, videosection_4__2, videosection_4__3, videosection_4__3_2, videosection_4__4,
       videosection_4__5, videosection_4__6, videosection_4__7;

  Button button_1 (.out(button_1_out));
  kinematic_controller kinematic_controller_1 (
    .leftbatY(not_1_out), .clock(clock_1_out), .reset(button_1_out), .ballX(kinematic_controller_1_ballx),
    .ballY(kinematic_controller_1_bally), .chipid(kinematic_controller_1_chipid),
    .leftbatY_2(kinematic_controller_1_leftbaty_2), .rightbatY(kinematic_controller_1_rightbaty));
  Joystick #(.bits(5)) joystick_1 (.y(joystick_1_y));  // open: x
  assign not_1_out = ~joystick_1_y;  // NOT_Gate not_1, 5 bits wide
  DotMatrix #(.matrixcols(32), .matrixrows(32)) dotmatrix_1 (
    .col0(videosection_1__1), .col1(videosection_1__2), .col2(videosection_1__3), .col3(videosection_1__3_2),
    .col4(videosection_1__4), .col5(videosection_1__5), .col6(videosection_1__6), .col7(videosection_1__7),
    .col8(videosection_2__1), .col9(videosection_2__2), .col10(videosection_2__3),
    .col11(videosection_2__3_2), .col12(videosection_2__4), .col13(videosection_2__5),
    .col14(videosection_2__6), .col15(videosection_2__7), .col16(videosection_3__1),
    .col17(videosection_3__2), .col18(videosection_3__3), .col19(videosection_3__3_2),
    .col20(videosection_3__4), .col21(videosection_3__5), .col22(videosection_3__6),
    .col23(videosection_3__7), .col24(videosection_4__1), .col25(videosection_4__2),
    .col26(videosection_4__3), .col27(videosection_4__3_2), .col28(videosection_4__4),
    .col29(videosection_4__5), .col30(videosection_4__6), .col31(videosection_4__7));
  Clock clock_1 (.out(clock_1_out));
  videoSection videosection_1 (
    .chipID(kinematic_controller_1_chipid), .ballX(kinematic_controller_1_ballx),
    .ballY(kinematic_controller_1_bally), .leftbatY(kinematic_controller_1_leftbaty_2),
    .rightbatY(kinematic_controller_1_rightbaty), .out_14(videosection_1_out_14),
    .out_15(videosection_1_out_15), .out_16(videosection_1_out_16), .out_17(videosection_1_out_17),
    .out_18(videosection_1_out_18), ._1(videosection_1__1), ._2(videosection_1__2), ._3(videosection_1__3),
    ._3_2(videosection_1__3_2), ._4(videosection_1__4), ._5(videosection_1__5), ._6(videosection_1__6),
    ._7(videosection_1__7));
  videoSection videosection_2 (
    .chipID(videosection_1_out_14), .ballX(videosection_1_out_15), .ballY(videosection_1_out_16),
    .leftbatY(videosection_1_out_17), .rightbatY(videosection_1_out_18), .out_14(videosection_2_out_14),
    .out_15(videosection_2_out_15), .out_16(videosection_2_out_16), .out_17(videosection_2_out_17),
    .out_18(videosection_2_out_18), ._1(videosection_2__1), ._2(videosection_2__2), ._3(videosection_2__3),
    ._3_2(videosection_2__3_2), ._4(videosection_2__4), ._5(videosection_2__5), ._6(videosection_2__6),
    ._7(videosection_2__7));
  videoSection videosection_3 (
    .chipID(videosection_2_out_14), .ballX(videosection_2_out_15), .ballY(videosection_2_out_16),
    .leftbatY(videosection_2_out_17), .rightbatY(videosection_2_out_18), .out_14(videosection_3_out_14),
    .out_15(videosection_3_out_15), .out_16(videosection_3_out_16), .out_17(videosection_3_out_17),
    .out_18(videosection_3_out_18), ._1(videosection_3__1), ._2(videosection_3__2), ._3(videosection_3__3),
    ._3_2(videosection_3__3_2), ._4(videosection_3__4), ._5(videosection_3__5), ._6(videosection_3__6),
    ._7(videosection_3__7));
  videoSection videosection_4 (
    .chipID(videosection_3_out_14), .ballX(videosection_3_out_15), .ballY(videosection_3_out_16),
    .leftbatY(videosection_3_out_17), .rightbatY(videosection_3_out_18), ._1(videosection_4__1),
    ._2(videosection_4__2), ._3(videosection_4__3), ._3_2(videosection_4__3_2), ._4(videosection_4__4),
    ._5(videosection_4__5), ._6(videosection_4__6), ._7(videosection_4__7));  // open: out_14, out_15, out_16, out_17, out_18
endmodule

module videoSection (
  input  [4:0] chipID,
  input  [4:0] ballX,
  input  [4:0] ballY,
  input  [4:0] leftbatY,
  input  [4:0] rightbatY,
  output [31:0] _1,
  output [31:0] _2,
  output [31:0] _3,
  output [31:0] _3_2,
  output [31:0] _4,
  output [31:0] _5,
  output [31:0] _6,
  output [31:0] _7,
  output [4:0] out_14,
  output [4:0] out_15,
  output [4:0] out_16,
  output [4:0] out_17,
  output [4:0] out_18
);

  wire [4:0] videochip_1_chip_id_out, videochip_1_out_7, videochip_1_out_8, videochip_1_out_9,
       videochip_1_out_11, videochip_2_chip_id_out, videochip_2_out_7, videochip_2_out_8, videochip_2_out_9,
       videochip_2_out_11, videochip_3_chip_id_out, videochip_3_out_7, videochip_3_out_8, videochip_3_out_9,
       videochip_3_out_11, videochip_4_chip_id_out, videochip_4_out_7, videochip_4_out_8, videochip_4_out_9,
       videochip_4_out_11, videochip_5_chip_id_out, videochip_5_out_7, videochip_5_out_8, videochip_5_out_9,
       videochip_5_out_11, videochip_6_chip_id_out, videochip_6_out_7, videochip_6_out_8, videochip_6_out_9,
       videochip_6_out_11, videochip_7_chip_id_out, videochip_7_out_7, videochip_7_out_8, videochip_7_out_9,
       videochip_7_out_11;

  videoChip videochip_1 (
    .chipID(chipID), .ballX(ballX), .ballY(ballY), .leftbatY(leftbatY), .rightbatY(rightbatY), .out(_1),
    .chip_id_out(videochip_1_chip_id_out), .out_11(videochip_1_out_11), .out_9(videochip_1_out_9),
    .out_8(videochip_1_out_8), .out_7(videochip_1_out_7));
  videoChip videochip_2 (
    .chipID(videochip_1_chip_id_out), .ballX(videochip_1_out_7), .ballY(videochip_1_out_8),
    .leftbatY(videochip_1_out_9), .rightbatY(videochip_1_out_11), .out(_2),
    .chip_id_out(videochip_2_chip_id_out), .out_11(videochip_2_out_11), .out_9(videochip_2_out_9),
    .out_8(videochip_2_out_8), .out_7(videochip_2_out_7));
  videoChip videochip_3 (
    .chipID(videochip_2_chip_id_out), .ballX(videochip_2_out_7), .ballY(videochip_2_out_8),
    .leftbatY(videochip_2_out_9), .rightbatY(videochip_2_out_11), .out(_3),
    .chip_id_out(videochip_3_chip_id_out), .out_11(videochip_3_out_11), .out_9(videochip_3_out_9),
    .out_8(videochip_3_out_8), .out_7(videochip_3_out_7));
  videoChip videochip_4 (
    .chipID(videochip_3_chip_id_out), .ballX(videochip_3_out_7), .ballY(videochip_3_out_8),
    .leftbatY(videochip_3_out_9), .rightbatY(videochip_3_out_11), .out(_3_2),
    .chip_id_out(videochip_4_chip_id_out), .out_11(videochip_4_out_11), .out_9(videochip_4_out_9),
    .out_8(videochip_4_out_8), .out_7(videochip_4_out_7));
  videoChip videochip_5 (
    .chipID(videochip_4_chip_id_out), .ballX(videochip_4_out_7), .ballY(videochip_4_out_8),
    .leftbatY(videochip_4_out_9), .rightbatY(videochip_4_out_11), .out(_4),
    .chip_id_out(videochip_5_chip_id_out), .out_11(videochip_5_out_11), .out_9(videochip_5_out_9),
    .out_8(videochip_5_out_8), .out_7(videochip_5_out_7));
  videoChip videochip_6 (
    .chipID(videochip_5_chip_id_out), .ballX(videochip_5_out_7), .ballY(videochip_5_out_8),
    .leftbatY(videochip_5_out_9), .rightbatY(videochip_5_out_11), .out(_5),
    .chip_id_out(videochip_6_chip_id_out), .out_11(videochip_6_out_11), .out_9(videochip_6_out_9),
    .out_8(videochip_6_out_8), .out_7(videochip_6_out_7));
  videoChip videochip_7 (
    .chipID(videochip_6_chip_id_out), .ballX(videochip_6_out_7), .ballY(videochip_6_out_8),
    .leftbatY(videochip_6_out_9), .rightbatY(videochip_6_out_11), .out(_6),
    .chip_id_out(videochip_7_chip_id_out), .out_11(videochip_7_out_11), .out_9(videochip_7_out_9),
    .out_8(videochip_7_out_8), .out_7(videochip_7_out_7));
  videoChip videochip_8 (
    .chipID(videochip_7_chip_id_out), .ballX(videochip_7_out_7), .ballY(videochip_7_out_8),
    .leftbatY(videochip_7_out_9), .rightbatY(videochip_7_out_11), .out(_7), .chip_id_out(out_14),
    .out_11(out_18), .out_9(out_17), .out_8(out_16), .out_7(out_15));
endmodule

module videoChip (
  input  [4:0] chipID,
  input  [4:0] ballX,
  input  [4:0] ballY,
  input  [4:0] leftbatY,
  input  [4:0] rightbatY,
  output [31:0] out,
  output [4:0] out_7,
  output [4:0] out_8,
  output [4:0] out_9,
  output [4:0] chip_id_out,
  output [4:0] out_11
);

  wire [31:0] cmpchipball_1_out, cmpchipball_2_out, cmpchipball_3_out, or_1_out, shifter_1_out, shifter_2_out;

  cmpChipBall cmpchipball_1 (.chipId(chipID), .ballX(ballX), .ballY(ballY), .out(cmpchipball_1_out));
  cmpChipBall cmpchipball_2 (.chipId(chipID), .ballX(5'b00011), .ballY(leftbatY), .out(cmpchipball_2_out));
  cmpChipBall cmpchipball_3 (.chipId(chipID), .ballX(5'b11100), .ballY(rightbatY), .out(cmpchipball_3_out));
  Adder #(.width(5)) adder_1 (.a(5'b00001), .b(chipID), .out(chip_id_out));  // open: cin, cout
  assign or_1_out = cmpchipball_2_out | cmpchipball_3_out;  // OR_Gate or_1, 32 bits wide
  Shifter #(.width(32)) shifter_1 (.in(or_1_out), .\dist (5'b00010), .out(shifter_1_out));
  Shifter #(.width(32)) shifter_2 (.in(or_1_out), .\dist (5'b00001), .out(shifter_2_out));
  assign out = cmpchipball_1_out | or_1_out | shifter_1_out | shifter_2_out;  // OR_Gate or_2, 32 bits wide

  assign out_7 = ballX;
  assign out_8 = ballY;
  assign out_9 = leftbatY;
  assign out_11 = rightbatY;

  // Other names for the same wires on the sheet: lBatY[4:0] = leftbatY; rBatY[4:0] = rightbatY
endmodule

module cmpChipBall (
  input  [4:0] ballY,
  input  [4:0] chipId,
  input  [4:0] ballX,
  output [31:0] out
);

  wire comparator_1_eq;

  // Probe on out
  Decoder #(.select(5), .disabled(0)) decoder_1 (
    .out0(out[0]), .out1(out[1]), .out2(out[2]), .out3(out[3]), .out4(out[4]), .out5(out[5]), .out6(out[6]),
    .out7(out[7]), .out8(out[8]), .out9(out[9]), .out10(out[10]), .out11(out[11]), .out12(out[12]),
    .out13(out[13]), .out14(out[14]), .out15(out[15]), .out16(out[16]), .out17(out[17]), .out18(out[18]),
    .out19(out[19]), .out20(out[20]), .out21(out[21]), .out22(out[22]), .out23(out[23]), .out24(out[24]),
    .out25(out[25]), .out26(out[26]), .out27(out[27]), .out28(out[28]), .out29(out[29]), .out30(out[30]),
    .out31(out[31]), .sel(ballY), .en(comparator_1_eq));
  Comparator #(.width(5)) comparator_1 (.a(chipId), .b(ballX), .eq(comparator_1_eq));  // open: gt, lt
endmodule

module mine (
  input  [7:0] bus_0,
  input  [7:0] bus_1,
  input  [7:0] bus_2,
  input  [7:0] bus_3,
  input  [1:0] bus_0_2,
  input  [2:0] bus_0_3
);

  wire [7:0] decoder_1_out0, multiplexer_1_out;

  Decoder #(.select(3), .disabled(0)) decoder_1 (
    .out0(decoder_1_out0[0]), .out1(decoder_1_out0[1]), .out2(decoder_1_out0[2]), .out3(decoder_1_out0[3]),
    .out4(decoder_1_out0[4]), .out5(decoder_1_out0[5]), .out6(decoder_1_out0[6]), .out7(decoder_1_out0[7]),
    .sel(bus_0_3));  // open: en
  Multiplexer #(.select(2), .width(8)) multiplexer_1 (
    .in0(bus_0), .in1(bus_1), .in2(bus_2), .in3(bus_3), .out(multiplexer_1_out), .sel(bus_0_2));  // open: en
  // Probe on multiplexer_1_out
  // Probe on decoder_1_out0
  // Probe on decoder_1_out0
endmodule

module kinematic_controller (
  input  reset,
  input  [4:0] leftbatY,
  input  clock,
  output [4:0] chipid,
  output [4:0] ballX,
  output [4:0] ballY,
  output [4:0] leftbatY_2,
  output [4:0] rightbatY
);

  wire and_1_out, and_2_out, d_ff_1_q, d_ff_1_qn, d_ff_2_q, d_ff_2_qn;
  wire [2:0] LongBallX, LongBallY;
  wire [7:0] adder_1_out, adder_2_out;

  D_Flip_Flop d_ff_1 (.clk(reset), .D(d_ff_1_qn), .Q(d_ff_1_q), .Qn(d_ff_1_qn));  // open: preset, en, reset
  D_Flip_Flop d_ff_2 (.clk(reset), .D(d_ff_2_qn), .Q(d_ff_2_q), .Qn(d_ff_2_qn));  // open: preset, en, reset
  Adder adder_1 (.a(8'h1), .b({ballX, LongBallX}), .out(adder_1_out));  // open: cin, cout
  and and_1 (and_1_out, d_ff_1_q, clock);
  Adder adder_2 (.a(8'h1), .b({ballY, LongBallY}), .out(adder_2_out));  // open: cin, cout
  and and_2 (and_2_out, d_ff_2_q, clock);
  Register register_1 (.D(adder_1_out), .Q({ballX, LongBallX}), .clk(and_1_out));  // open: en, clr
  Register register_2 (.D(adder_2_out), .Q({ballY, LongBallY}), .clk(and_2_out));  // open: en, clr

  assign chipid = {5{1'b0}};
  assign leftbatY_2 = leftbatY;
  assign rightbatY = {5{1'b0}};

  // Other names for the same wires on the sheet: LongBallX[7:3] = ballX; LongBallY[7:3] = ballY
endmodule
